# Fritzing sketch schema_v1 (saved by Fritzing 1.0.4)

parts:
  Mod1 = Raspberry Pi 4B
  M1 = Arduino NANO RP2040 CONNECT with headers
  U1 = GAS_SENSOR [package=mq-3]
  RHT1 = Humidity and Temperature Sensor RHT03
  R1 = Resistor [tolerance=±5% resistance=10k package="1206 [SMD]"]
  M2 = RioRand LM2596  # not connected

nets:
  5V: Mod1.5V, M1.VIN, U1.B1, U1.H2
  N1: Mod1.GND, M1.GND-4, M1.GND-29, U1.A1, U1.H1
  N2: Mod1.GPIO14, M1.D2
  N3: Mod1.GPIO15, M1.D3
  N4: Mod1.GPIO18, M1.D4
  N5: Mod1.GPIO23, M1.D5
  N6: Mod1.GPIO10, M1.D6
  N7: Mod1.GPIO9, M1.D7
  N8: Mod1.GPIO11, M1.D8
  N9: M1.D13, RHT1.Vcc
  N10: M1.AREF, RHT1.Data-signal
  N11: M1.RESET-28, RHT1.GND_1, RHT1.GND_2, R1.Pin_0
